# Fritzing sketch FinalHomeWork (saved by Fritzing 0.9.3b)
breadboards: 1

parts:
  LED1 = LED - 3mm [color="Red (633nm)" package="3 mm [THT]"]
  R2 = Resistor [tolerance=±5% resistance=330 package="2010 [SMD]"]
  Part1 = Arduino Uno (Rev3) - ICSP
  R3 = Textile Potentiometer [part_number=PW064]
  R4 = Resistor [tolerance=±5% resistance=10k package="2010 [SMD]"]
  R5 = PHOTOCELL [package=photocell]
  R6 = Resistor [tolerance=±5% resistance=10k package="2010 [SMD]"]
  J1 = Piezo Speaker
  R7 = Resistor [tolerance=±5% resistance=330 package="2010 [SMD]"]

nets:
  N1: LED1.cathode, R2.Pin_1
  N2: LED1.anode, Part1.D8, Part1.D9_PWM
  N3: R2.Pin_0, Part1.GND, R3.leg1, R6.Pin_1
  N4: Part1.A0, R5.P$2, R6.Pin_0
  N5: Part1.A1, R3.wiper, R4.Pin_1
  N6: Part1.5V, R3.leg2, R4.Pin_0, R5.P$1, R7.Pin_0
  N7: Part1.D10_PWM/SS, J1.pin1
  N8: J1.pin2, R7.Pin_1
